# Fritzing sketch DockDeck_v1.1 (saved by Fritzing 0.9.3b)
breadboards: 1

parts:
  Composant1 = Arduino Pro Mini v13
  S1 = Momentary Switch [package=ksa_sealed_tac_switch]
  S2 = Momentary Switch [package=ksa_sealed_tac_switch]
  R1 = Resistor [tolerance=±5% resistance=1k package="0402 [SMD]"]
  R2 = Resistor [tolerance=±5% resistance=1k package="0402 [SMD]"]
  R3 = Resistor [tolerance=±5% resistance=1k package="0402 [SMD]"]
  LED1 = smd LED [color="Red (633nm)" package="0805 [SMD]"]
  S3 = Momentary Switch [package=ksa_sealed_tac_switch]
  R4 = Resistor [tolerance=±5% resistance=1k package="0402 [SMD]"]
  S4 = Momentary Switch [package=ksa_sealed_tac_switch]
  R5 = Resistor [tolerance=±5% resistance=1k package="0402 [SMD]"]
  LED2 = smd LED [color="Green (555nm)" package="0805 [SMD]"]
  R6 = Resistor [tolerance=±5% resistance=1k package="0402 [SMD]"]

nets:
  N1: Composant1.GND, Composant1.D0/TX, R1.Pin_1, R2.Pin_1, R3.Pin_0, R4.Pin_1, R5.Pin_1, R6.Pin_0
  N2: Composant1.VCC, S1.4, S2.4, S3.4, S4.4
  N3: Composant1.D9_PWM, S4.1
  N4: Composant1.D8, S3.1
  N5: Composant1.D7, S2.1
  N6: Composant1.D6_PWM, S1.1
  N7: Composant1.D5_PWM, LED1.cathode
  N8: Composant1.D4, R3.Pin_1, LED1.anode
  N9: Composant1.D3_PWM, LED2.cathode
  N10: Composant1.D2, LED2.anode, R6.Pin_1
  N11: S1.2, R1.Pin_0
  N12: S2.2, R2.Pin_0
  N13: S3.2, R4.Pin_0
  N14: S4.2, R5.Pin_0
